# Fritzing sketch 7688-photocellfzz (saved by Fritzing 0.9.3b)
breadboards: 1

parts:
  Part1 = LinkIt Smart 7688 Duo
  R1 = Resistor [tolerance=±5% resistance=220 package=THT]
  R2 = Photocell (LDR) [package=THT]

nets:
  N1: Part1.GND, R2.pin_1
  N2: Part1.3V3, R1.Pin_0
  N3: Part1.A0, R1.Pin_1, R2.pin_0

custom parts:
  LinkIt Smart 7688 Duo: At the heart of the platform is the MT7688AN SOC, an appliance automation bridge. This chipset is based on a powerful 802.11n 1T1R Wi-Fi AP, supports up to 2Gb RAM with additional SD-card storage, encryption engine Wi-Fi and a wide variety of peripheral connectivity options.
